// Logisim project Eclipse-10000.circ as structural Verilog
module AddSub16bit (
  input  in_1,
  input  [15:0] in_2,
  input  [15:0] in_3,
  output [15:0] out_4,
  output out_5
);

  wire and_1_out, and_2_out, and_3_out, and_4_out, and_5_out, and_6_out, and_7_out, and_8_out, and_9_out,
       and_10_out, and_11_out, and_12_out, and_13_out, and_14_out, and_15_out, and_16_out, and_17_out,
       and_18_out, and_19_out, and_20_out, and_21_out, and_22_out, and_23_out, and_24_out, and_25_out,
       and_26_out, and_27_out, and_28_out, and_29_out, and_30_out, and_31_out, and_32_out, or_1_out,
       or_2_out, or_3_out, or_4_out, or_5_out, or_6_out, or_7_out, or_8_out, or_9_out, or_10_out, or_11_out,
       or_12_out, or_13_out, or_14_out, or_15_out, xor_2_out, xor_3_out, xor_4_out, xor_5_out, xor_10_out,
       xor_11_out, xor_12_out, xor_13_out, xor_18_out, xor_19_out, xor_20_out, xor_21_out, xor_26_out,
       xor_27_out, xor_28_out, xor_29_out;
  wire [15:0] bit_extender_1_out, xor_1_out;

  assign bit_extender_1_out = {{15{in_1}}, in_1};  // Bit_Extender bit_extender_1
  assign xor_1_out = bit_extender_1_out ^ in_3;  // XOR_Gate xor_1, 16 bits wide
  xor xor_2 (xor_2_out, in_2[0], xor_1_out[0]);
  xor xor_3 (xor_3_out, in_2[4], xor_1_out[4]);
  xor xor_4 (xor_4_out, in_2[8], xor_1_out[8]);
  xor xor_5 (xor_5_out, in_2[12], xor_1_out[12]);
  xor xor_6 (out_4[0], xor_2_out, in_1);
  and and_1 (and_1_out, xor_2_out, in_1);
  and and_2 (and_2_out, in_2[0], xor_1_out[0]);
  xor xor_7 (out_4[4], xor_3_out, or_13_out);
  and and_3 (and_3_out, xor_3_out, or_13_out);
  and and_4 (and_4_out, in_2[4], xor_1_out[4]);
  xor xor_8 (out_4[8], xor_4_out, or_14_out);
  and and_5 (and_5_out, xor_4_out, or_14_out);
  and and_6 (and_6_out, in_2[8], xor_1_out[8]);
  xor xor_9 (out_4[12], xor_5_out, or_15_out);
  and and_7 (and_7_out, xor_5_out, or_15_out);
  and and_8 (and_8_out, in_2[12], xor_1_out[12]);
  or or_1 (or_1_out, and_1_out, and_2_out);
  or or_2 (or_2_out, and_3_out, and_4_out);
  or or_3 (or_3_out, and_5_out, and_6_out);
  or or_4 (or_4_out, and_7_out, and_8_out);
  xor xor_10 (xor_10_out, in_2[1], xor_1_out[1]);
  xor xor_11 (xor_11_out, in_2[5], xor_1_out[5]);
  xor xor_12 (xor_12_out, in_2[9], xor_1_out[9]);
  xor xor_13 (xor_13_out, in_2[13], xor_1_out[13]);
  xor xor_14 (out_4[1], xor_10_out, or_1_out);
  and and_9 (and_9_out, xor_10_out, or_1_out);
  and and_10 (and_10_out, in_2[1], xor_1_out[1]);
  xor xor_15 (out_4[5], xor_11_out, or_2_out);
  and and_11 (and_11_out, xor_11_out, or_2_out);
  and and_12 (and_12_out, in_2[5], xor_1_out[5]);
  xor xor_16 (out_4[9], xor_12_out, or_3_out);
  and and_13 (and_13_out, xor_12_out, or_3_out);
  and and_14 (and_14_out, in_2[9], xor_1_out[9]);
  xor xor_17 (out_4[13], xor_13_out, or_4_out);
  and and_15 (and_15_out, xor_13_out, or_4_out);
  and and_16 (and_16_out, in_2[13], xor_1_out[13]);
  or or_5 (or_5_out, and_9_out, and_10_out);
  or or_6 (or_6_out, and_11_out, and_12_out);
  or or_7 (or_7_out, and_13_out, and_14_out);
  or or_8 (or_8_out, and_15_out, and_16_out);
  xor xor_18 (xor_18_out, in_2[2], xor_1_out[2]);
  xor xor_19 (xor_19_out, in_2[6], xor_1_out[6]);
  xor xor_20 (xor_20_out, in_2[10], xor_1_out[10]);
  xor xor_21 (xor_21_out, in_2[14], xor_1_out[14]);
  xor xor_22 (out_4[2], xor_18_out, or_5_out);
  and and_17 (and_17_out, xor_18_out, or_5_out);
  and and_18 (and_18_out, in_2[2], xor_1_out[2]);
  xor xor_23 (out_4[6], xor_19_out, or_6_out);
  and and_19 (and_19_out, xor_19_out, or_6_out);
  and and_20 (and_20_out, in_2[6], xor_1_out[6]);
  xor xor_24 (out_4[10], xor_20_out, or_7_out);
  and and_21 (and_21_out, xor_20_out, or_7_out);
  and and_22 (and_22_out, in_2[10], xor_1_out[10]);
  xor xor_25 (out_4[14], xor_21_out, or_8_out);
  and and_23 (and_23_out, xor_21_out, or_8_out);
  and and_24 (and_24_out, in_2[14], xor_1_out[14]);
  or or_9 (or_9_out, and_17_out, and_18_out);
  or or_10 (or_10_out, and_19_out, and_20_out);
  or or_11 (or_11_out, and_21_out, and_22_out);
  or or_12 (or_12_out, and_23_out, and_24_out);
  xor xor_26 (xor_26_out, in_2[3], xor_1_out[3]);
  xor xor_27 (xor_27_out, in_2[7], xor_1_out[7]);
  xor xor_28 (xor_28_out, in_2[11], xor_1_out[11]);
  xor xor_29 (xor_29_out, in_2[15], xor_1_out[15]);
  xor xor_30 (out_4[3], xor_26_out, or_9_out);
  and and_25 (and_25_out, xor_26_out, or_9_out);
  and and_26 (and_26_out, in_2[3], xor_1_out[3]);
  xor xor_31 (out_4[7], xor_27_out, or_10_out);
  and and_27 (and_27_out, xor_27_out, or_10_out);
  and and_28 (and_28_out, in_2[7], xor_1_out[7]);
  xor xor_32 (out_4[11], xor_28_out, or_11_out);
  and and_29 (and_29_out, xor_28_out, or_11_out);
  and and_30 (and_30_out, in_2[11], xor_1_out[11]);
  xor xor_33 (out_4[15], xor_29_out, or_12_out);
  and and_31 (and_31_out, xor_29_out, or_12_out);
  and and_32 (and_32_out, in_2[15], xor_1_out[15]);
  or or_13 (or_13_out, and_25_out, and_26_out);
  or or_14 (or_14_out, and_27_out, and_28_out);
  or or_15 (or_15_out, and_29_out, and_30_out);
  or or_16 (out_5, and_31_out, and_32_out);
endmodule

module SubAdder4bit (
  input  [3:0] X,
  input  [3:0] Y,
  input  isSub,
  input  Cin,
  output [3:0] Result,
  output PG,
  output GG
);

  wire and_1_out, and_2_out, and_3_out, and_4_out, and_6_out, and_7_out, and_8_out, and_9_out, and_10_out,
       and_11_out, and_12_out, and_13_out, and_14_out, or_1_out, or_3_out, or_4_out, xor_2_out, xor_3_out,
       xor_4_out, xor_5_out;
  wire [3:0] bit_extender_1_out, xor_1_out;

  assign bit_extender_1_out = {{3{isSub}}, isSub};  // Bit_Extender bit_extender_1
  assign xor_1_out = Y ^ bit_extender_1_out;  // XOR_Gate xor_1, 4 bits wide
  xor xor_2 (xor_2_out, xor_1_out[0], X[0]);
  and and_1 (and_1_out, X[0], xor_1_out[0]);
  xor xor_3 (xor_3_out, xor_1_out[1], X[1]);
  and and_2 (and_2_out, X[1], xor_1_out[1]);
  xor xor_4 (xor_4_out, xor_1_out[2], X[2]);
  and and_3 (and_3_out, X[2], xor_1_out[2]);
  xor xor_5 (xor_5_out, xor_1_out[3], X[3]);
  and and_4 (and_4_out, X[3], xor_1_out[3]);
  xor xor_6 (Result[0], Cin, xor_2_out);
  xor xor_7 (Result[1], or_1_out, xor_3_out);
  xor xor_8 (Result[2], or_3_out, xor_4_out);
  xor xor_9 (Result[3], or_4_out, xor_5_out);
  or or_1 (or_1_out, and_1_out, and_12_out);
  or or_2 (GG, and_4_out, and_9_out, and_10_out, and_11_out);
  or or_3 (or_3_out, and_2_out, and_6_out, and_7_out);
  or or_4 (or_4_out, and_3_out, and_13_out, and_14_out, and_8_out);
  and and_5 (PG, xor_5_out, xor_4_out, xor_3_out, xor_2_out);
  and and_6 (and_6_out, xor_3_out, and_1_out);
  and and_7 (and_7_out, xor_3_out, xor_2_out, Cin);
  and and_8 (and_8_out, xor_4_out, xor_3_out, xor_2_out, Cin);
  and and_9 (and_9_out, xor_5_out, and_3_out);
  and and_10 (and_10_out, xor_5_out, xor_4_out, and_2_out);
  and and_11 (and_11_out, xor_5_out, xor_4_out, xor_3_out, and_1_out);
  and and_12 (and_12_out, Cin, xor_2_out);
  and and_13 (and_13_out, xor_4_out, and_2_out);
  and and_14 (and_14_out, xor_4_out, xor_3_out, and_1_out);
endmodule

module ALU (
  input  [15:0] Y,
  input  [15:0] X,
  input  [3:0] opcode,
  output [15:0] Result
);

  wire decoder4_16_1_sub_0100;
  wire [15:0] and_1_out, and_2_out, and_3_out, and_4_out, and_5_out, and_6_out, and_7_out,
       bit_extender_1_out, decoder4_16_1_add_0000, decoder4_16_1_and_0010, decoder4_16_1_not_0101,
       decoder4_16_1_or_0001, decoder4_16_1_xor_0011, not_1_out, or_1_out, subadder16bit_1_result,
       subadder16bit_2_result, xor_1_out;

  Decoder4_16 decoder4_16_1 (
    .opcode(opcode), .Add_0000(decoder4_16_1_add_0000), .Sub_0100(decoder4_16_1_sub_0100),
    .XOR_0011(decoder4_16_1_xor_0011), .OR_0001(decoder4_16_1_or_0001), .AND_0010(decoder4_16_1_and_0010),
    .NOT_0101(decoder4_16_1_not_0101));  // open: out_8, out_9, out_10, out_11, out_12, out_13, out_14, out_15, out_16, out_17
  SubAdder16bit subadder16bit_1 (.X(X), .Y(Y), .Result(subadder16bit_1_result));  // open: isSub, OverflowFlag
  assign and_1_out = decoder4_16_1_add_0000 & subadder16bit_1_result;  // AND_Gate and_1, 16 bits wide
  SubAdder16bit subadder16bit_2 (
    .X(X), .Y(Y), .isSub(decoder4_16_1_sub_0100), .Result(subadder16bit_2_result));  // open: OverflowFlag
  assign bit_extender_1_out = {{15{decoder4_16_1_sub_0100}}, decoder4_16_1_sub_0100};  // Bit_Extender bit_extender_1
  assign and_2_out = bit_extender_1_out & subadder16bit_2_result;  // AND_Gate and_2, 16 bits wide
  assign or_1_out = Y | X;  // OR_Gate or_1, 16 bits wide
  assign xor_1_out = Y ^ X;  // XOR_Gate xor_1, 16 bits wide
  assign and_3_out = decoder4_16_1_xor_0011 & xor_1_out;  // AND_Gate and_3, 16 bits wide
  assign and_4_out = decoder4_16_1_or_0001 & or_1_out;  // AND_Gate and_4, 16 bits wide
  assign Result = and_2_out | and_1_out | and_3_out | and_4_out | and_6_out | and_7_out;  // OR_Gate or_2, 16 bits wide
  assign and_5_out = Y & X;  // AND_Gate and_5, 16 bits wide
  assign and_6_out = decoder4_16_1_and_0010 & and_5_out;  // AND_Gate and_6, 16 bits wide
  assign not_1_out = ~X;  // NOT_Gate not_1, 16 bits wide
  assign and_7_out = decoder4_16_1_not_0101 & not_1_out;  // AND_Gate and_7, 16 bits wide
endmodule

module Decoder4_16 (
  input  [3:0] opcode,
  output [15:0] Add_0000,
  output Sub_0100,
  output [15:0] XOR_0011,
  output [15:0] OR_0001,
  output [15:0] AND_0010,
  output [15:0] NOT_0101,
  output out_8,
  output out_9,
  output out_10,
  output out_11,
  output out_12,
  output out_13,
  output out_14,
  output out_15,
  output out_16,
  output out_17
);

  wire and_1_out, and_3_out, and_4_out, and_5_out, and_6_out, not_1_out, not_2_out, not_3_out, not_4_out,
       not_5_out, not_6_out, not_7_out, not_8_out, not_9_out, not_10_out, not_11_out, not_12_out, not_14_out,
       not_15_out, not_16_out, not_17_out, not_18_out, not_19_out, not_20_out, not_21_out, not_22_out,
       not_23_out, not_24_out, not_25_out, not_26_out, not_27_out, not_28_out, not_29_out, not_30_out,
       not_31_out, not_32_out;

  not not_1 (not_1_out, opcode[0]);
  not not_2 (not_2_out, opcode[1]);
  and and_1 (and_1_out, not_1_out, not_2_out, not_3_out, not_4_out);
  not not_3 (not_3_out, opcode[2]);
  not not_4 (not_4_out, opcode[3]);
  not not_5 (not_5_out, opcode[0]);
  not not_6 (not_6_out, opcode[1]);
  and and_2 (Sub_0100, not_5_out, not_6_out, opcode[2], not_7_out);
  not not_7 (not_7_out, opcode[3]);
  and and_3 (and_3_out, opcode[0], opcode[1], not_8_out, not_9_out);
  not not_8 (not_8_out, opcode[2]);
  not not_9 (not_9_out, opcode[3]);
  not not_10 (not_10_out, opcode[1]);
  and and_4 (and_4_out, opcode[0], not_10_out, not_11_out, not_12_out);
  not not_11 (not_11_out, opcode[2]);
  not not_12 (not_12_out, opcode[3]);
  // NOT_Gate not_13 has open pins: in=opcode[0], out=open
  and and_5 (and_5_out, opcode[1], not_14_out, not_15_out);
  not not_14 (not_14_out, opcode[2]);
  not not_15 (not_15_out, opcode[3]);
  not not_16 (not_16_out, opcode[1]);
  and and_6 (and_6_out, opcode[0], not_16_out, opcode[2], not_17_out);
  not not_17 (not_17_out, opcode[3]);
  and and_7 (out_8, opcode[0], opcode[1], opcode[2], not_18_out);
  not not_18 (not_18_out, opcode[3]);
  not not_19 (not_19_out, opcode[1]);
  and and_8 (out_9, opcode[0], not_19_out, not_20_out, opcode[3]);
  not not_20 (not_20_out, opcode[2]);
  not not_21 (not_21_out, opcode[0]);
  and and_9 (out_10, not_21_out, opcode[1], opcode[2], not_22_out);
  not not_22 (not_22_out, opcode[3]);
  and and_10 (out_11, opcode[0], opcode[1], not_23_out, opcode[3]);
  not not_23 (not_23_out, opcode[2]);
  not not_24 (not_24_out, opcode[0]);
  not not_25 (not_25_out, opcode[1]);
  and and_11 (out_12, not_24_out, not_25_out, opcode[2], opcode[3]);
  not not_26 (not_26_out, opcode[0]);
  and and_12 (out_13, not_26_out, opcode[1], opcode[2], opcode[3]);
  not not_27 (not_27_out, opcode[1]);
  and and_13 (out_14, opcode[0], not_27_out, opcode[2], opcode[3]);
  not not_28 (not_28_out, opcode[0]);
  and and_14 (out_15, not_28_out, opcode[1], not_29_out, opcode[3]);
  not not_29 (not_29_out, opcode[2]);
  not not_30 (not_30_out, opcode[0]);
  not not_31 (not_31_out, opcode[1]);
  and and_15 (out_16, not_30_out, not_31_out, not_32_out, opcode[3]);
  not not_32 (not_32_out, opcode[2]);
  and and_16 (out_17, opcode[0], opcode[1], opcode[2], opcode[3]);
  assign Add_0000 = {{15{and_1_out}}, and_1_out};  // Bit_Extender bit_extender_1
  assign XOR_0011 = {{15{and_3_out}}, and_3_out};  // Bit_Extender bit_extender_2
  assign OR_0001 = {{15{and_4_out}}, and_4_out};  // Bit_Extender bit_extender_3
  assign AND_0010 = {{15{and_5_out}}, and_5_out};  // Bit_Extender bit_extender_4
  assign NOT_0101 = {{15{and_6_out}}, and_6_out};  // Bit_Extender bit_extender_5
endmodule

module SubAdder16bit (
  input  [15:0] X,
  input  [15:0] Y,
  input  isSub,
  output [15:0] Result,
  output OverflowFlag
);

  wire and_1_out, and_2_out, and_3_out, and_4_out, and_5_out, and_6_out, and_7_out, and_8_out, and_9_out,
       and_10_out, or_1_out, or_2_out, or_3_out, or_4_out, subadder4bit_1_gg, subadder4bit_1_pg,
       subadder4bit_2_gg, subadder4bit_2_pg, subadder4bit_3_gg, subadder4bit_3_pg, subadder4bit_4_gg,
       subadder4bit_4_pg;

  xor xor_1 (OverflowFlag, isSub, or_2_out);
  SubAdder4bit subadder4bit_1 (
    .X(X[3:0]), .Y(Y[3:0]), .isSub(isSub), .Cin(isSub), .Result(Result[3:0]), .PG(subadder4bit_1_pg),
    .GG(subadder4bit_1_gg));
  SubAdder4bit subadder4bit_2 (
    .X(X[7:4]), .Y(Y[7:4]), .isSub(isSub), .Cin(or_3_out), .Result(Result[7:4]), .PG(subadder4bit_2_pg),
    .GG(subadder4bit_2_gg));
  SubAdder4bit subadder4bit_3 (
    .X(X[11:8]), .Y(Y[11:8]), .isSub(isSub), .Cin(or_4_out), .Result(Result[11:8]), .PG(subadder4bit_3_pg),
    .GG(subadder4bit_3_gg));
  or or_1 (or_1_out, subadder4bit_3_gg, and_1_out, and_2_out, and_3_out);
  SubAdder4bit subadder4bit_4 (
    .X(X[15:12]), .Y(Y[15:12]), .isSub(isSub), .Cin(or_1_out), .Result(Result[15:12]),
    .PG(subadder4bit_4_pg), .GG(subadder4bit_4_gg));
  or or_2 (or_2_out, subadder4bit_4_gg, and_4_out, and_5_out, and_6_out, and_7_out);
  or or_3 (or_3_out, subadder4bit_1_gg, and_8_out);
  or or_4 (or_4_out, subadder4bit_2_gg, and_9_out, and_10_out);
  and and_1 (and_1_out, subadder4bit_3_pg, subadder4bit_2_gg);
  and and_2 (and_2_out, subadder4bit_1_gg, subadder4bit_2_pg, subadder4bit_3_pg);
  and and_3 (and_3_out, subadder4bit_3_pg, subadder4bit_2_pg, subadder4bit_1_pg, isSub);
  and and_4 (and_4_out, subadder4bit_3_gg, subadder4bit_4_pg);
  and and_5 (and_5_out, subadder4bit_2_gg, subadder4bit_3_pg, subadder4bit_4_pg);
  and and_6 (and_6_out, subadder4bit_4_pg, subadder4bit_2_pg, subadder4bit_1_gg, subadder4bit_3_pg);
  and and_7 (and_7_out, subadder4bit_4_pg, subadder4bit_3_pg, subadder4bit_2_pg, subadder4bit_1_pg, isSub);
  and and_8 (and_8_out, isSub, subadder4bit_1_pg);
  and and_9 (and_9_out, subadder4bit_1_gg, subadder4bit_2_pg);
  and and_10 (and_10_out, subadder4bit_2_pg, subadder4bit_1_pg, isSub);
endmodule
